# Fritzing sketch temp_humidity_expanded (saved by Fritzing 0.9.3b)
circuit board: 8.46667cm x 5.64444cm
breadboards: 1

parts:
  LCD1 = LCD screen
  R1 = Resistor [tolerance=±5% resistance=220 package=THT]
  R2 = Resistor [tolerance=±5% resistance=220 package=THT]
  R3 = Resistor [tolerance=±5% resistance=220 package=THT]
  LED1 = LED - 5mm [color="Blue (430nm)" package="5 mm [THT]"]
  LED2 = LED - 5mm [color="Green (555nm)" package="5 mm [THT]"]
  LED3 = LED - 5mm [color="Red (633nm)" package="5 mm [THT]"]
  Part1 = Arduino Uno (Rev3)
  R5 = Trimmer Potentiometer [maximum_resistance=10kΩ package=THT]

nets:
  VSS: LCD1.VSS, LCD1.R/W, LCD1.LED-, LED1.cathode, LED2.cathode, LED3.cathode, Part1.GND, R5.leg2
  VDD: LCD1.VDD, LCD1.LED+, Part1.5V, R5.leg1
  N1: LCD1.V0, R5.wiper
  N2: LCD1.RS, Part1.D7
  N3: LCD1.E, Part1.D8
  N4: LCD1.DB4, Part1.D9_PWM
  N5: LCD1.DB5, Part1.D10_PWM/SS
  N6: LCD1.DB6, Part1.D11_PWM/MOSI
  N7: LCD1.DB7, Part1.D12/MISO
  N8: R1.Pin_0, Part1.D6_PWM
  N9: R1.Pin_1, LED1.anode
  N10: R2.Pin_0, Part1.D5_PWM
  N11: R2.Pin_1, LED2.anode
  N12: R3.Pin_0, Part1.D4
  N13: R3.Pin_1, LED3.anode
